# Fritzing sketch RGB Temperature (saved by Fritzing 0.9.3b)
breadboards: 1

parts:
  Arduino_UNO = Arduino Uno (Rev3)
  R1 = Resistor [tolerance=±5% resistance=360 package=THT]
  R2 = Resistor [tolerance=±5% resistance=360 package=THT]
  R3 = Resistor [tolerance=±5% resistance=360 package=THT]
  DS1 = DS18B20 1-Wire Temperature Sensor [part_number=DS18B20]
  R4 = Resistor [tolerance=±5% resistance=4.7k package=THT]
  LED1 = RGB LED (com. cathode, rgb) [package="5 mm [THT]"]

nets:
  N1: Arduino_UNO.D9_PWM, R1.Pin_1
  N2: Arduino_UNO.D10_PWM/SS, R2.Pin_1
  N3: Arduino_UNO.D11_PWM/MOSI, R3.Pin_1
  N4: Arduino_UNO.D2, DS1.DQ, R4.Pin_0
  5V: Arduino_UNO.5V, DS1.VDD, R4.Pin_1
  GND: Arduino_UNO.GND, DS1.GND, LED1.green_anode
  N5: R1.Pin_0, LED1.red_anode
  N6: R2.Pin_0, LED1.common_cathode
  N7: R3.Pin_0, LED1.blue_anode
